# Fritzing sketch Circuit_Diagram (saved by Fritzing 0.9.3b)
breadboards: 1

parts:
  Parça1 = Arduino Uno (Rev3) - ICSP
  LED1 = RGB LED (com. cathode, rgb) [package="5 mm [THT]"]
  R1 = Resistor [tolerance=±5% resistance=220 package="0402 [SMD]"]
  R2 = Resistor [tolerance=±5% resistance=220 package="0402 [SMD]"]
  R3 = Resistor [tolerance=±5% resistance=220 package="0402 [SMD]"]
  Q1 = TRANSISTOR_NPN [package=to-92-ammo]
  Q2 = TRANSISTOR_NPN [package=to-92-ammo]
  M1 = DC Motor
  M2 = DC Motor
  C4 = Capacitor Polarized [package=cpol-radial-100uf-25v]
  C5 = Capacitor Polarized [package=cpol-radial-100uf-25v]
  R4 = Resistor [tolerance=±5% resistance=220 package=THT]
  R5 = Resistor [tolerance=±5% resistance=220 package=THT]
  D1 = Diode [package=diode-1n4001]
  D2 = Diode [package=diode-1n4001]
  RHT1 = Humidity and Temperature Sensor RHT03

nets:
  N1: Parça1.D3_PWM, R4.Pin_1
  N2: Parça1.D5_PWM, R5.Pin_1
  N3: Parça1.D7, RHT1.Data-signal
  N4: LED1.red_anode, R3.Pin_0
  N5: LED1.common_cathode, R2.Pin_0
  N6: LED1.green_anode, M1.pin_1, M2.pin_1, D1.C, D2.C, RHT1.Vcc
  N7: LED1.blue_anode, R1.Pin_0
  N8: Q1.E, Q2.E, C4.-, C5.-, RHT1.GND_2
  N9: Q1.B, M1.pin_2
  N10: Q1.C, C4.+, R4.Pin_0
  N11: Q2.B, M2.pin_2
  N12: Q2.C, C5.+, R5.Pin_0

notes:
  RGB LED
  DHT11
  10uF
  Kondansatörler
  PWM 9 -->R
  PWM10-->G
  PWM11-->B
  (RGB LED )
  PWM 3-->M1
  PWM 5-->M2
  (DC motors )
  PWM 7-->Data
  (DHT11 )
  330 ohm
  Dirençler
  M1
  M2
